# Fritzing sketch Sub_Osc_Interface (saved by Fritzing 0.9.4)
breadboards: 1

parts:
  IC1 = Dual Op-Amp [package=dip08]
  R1 = Resistor [tolerance=±5% resistance=10k package=THT]
  R2 = Resistor [tolerance=±5% resistance=1k package=THT]
  R3 = Resistor [tolerance=±5% resistance=1.8k package=THT]
  C1 = Electrolytic Capacitor [capacitance=1µF package="100 mil [THT, electrolytic]"]
  R6 = Resistor [tolerance=±5% resistance=220 package=THT]
  D1 = Rectifier Diode [part_number=1N4001 package="300 mil [THT]"]
  C2 = Ceramic Capacitor [capacitance=100nF package="100 mil [THT, multilayer]"]
  C3 = Ceramic Capacitor [capacitance=100nF package="100 mil [THT, multilayer]"]
  C4 = Electrolytic Capacitor [capacitance=1µF package="100 mil [THT, electrolytic]"]
  C5 = Electrolytic Capacitor [capacitance=1µF package="100 mil [THT, electrolytic]"]

nets:
  N1: IC1.A_OUT, R6.Pin_1
  N2: IC1.A_-IN, R1.Pin_0, D1.anode, C2.1, C3.1, C4.+, C5.-
  N3: IC1.A_V-, C2.0, C4.-
  N4: IC1.B_+IN, R1.Pin_1, R3.Pin_0
  N5: IC1.B_-IN, IC1.B_OUT, R2.Pin_1
  N6: IC1.A_V+, C3.0, C5.+
  N7: R3.Pin_1, C1.-
  N8: R6.Pin_0, D1.cathode

notes:
  Out Stage
  Input
  +12V SQR
  Out Stage
  Output
  In Stage
  Output
  In Stage
  Input
  +/-5V SQR
  GND
  +12V
  -12V
  GND
